// Logisim project libshow.circ as structural Verilog
module main (
  input  in_1
);

  _7_Segment_Display u_7_segment_display_1 (.f(in_1), .a(in_1), .b(in_1), .e(in_1), .d(in_1), .c(in_1));  // open: g, dp
  _7_Segment_Display u_7_segment_display_2 (.f(in_1), .e(in_1));  // open: g, a, b, d, c, dp

  // Notes on the sheet:
  //   Biblioteca de Circuitos - Logisim$812839 - Vinícius Miranda de Araújo$$Os circuitos estão separados por categorias o arquivo separadores são "______Name" e$os circuitos seguintes são referentes a essa categoria.
endmodule

// MUX
module MUX_2x1 (
  input  I0,
  input  I1,
  input  A1,
  output S0
);

  wire AND1_out, AND2_out, not_1_out;

  and AND1 (AND1_out, I0, not_1_out);
  not not_1 (not_1_out, A1);
  and AND2 (AND2_out, I1, A1);
  or OR1 (S0, AND1_out, AND2_out);

  // Notes on the sheet:
  //   Multiplexador 2x1
endmodule

// MUX
module MUX_4x2 (
  input  A1,
  input  A0,
  input  I1,
  input  I2,
  input  I3,
  input  I4,
  output S0
);

  wire AND1_out, AND2_out, AND3_out, AND4_out, not_1_out, not_2_out;

  not not_1 (not_1_out, A1);
  not not_2 (not_2_out, A0);
  and AND1 (AND1_out, not_2_out, not_1_out, I1);
  and AND2 (AND2_out, A0, not_1_out, I2);
  and AND3 (AND3_out, not_2_out, A1, I3);
  and AND4 (AND4_out, A0, A1, I4);
  or OR1 (S0, AND1_out, AND2_out, AND3_out, AND4_out);

  // Notes on the sheet:
  //   Multiplexador 4x2
endmodule

// MUX
module MUX_8x3 (
  input  A2,
  input  A1,
  input  A0,
  input  I0,
  input  I1,
  input  I2,
  input  I3,
  input  I4,
  input  I5,
  input  I6,
  input  I7,
  output S0
);

  wire AND1_out, AND2_out, AND3_out, AND4_out, AND5_out, AND6_out, AND7_out, AND8_out, not_1_out, not_2_out,
       not_3_out;

  not not_1 (not_1_out, A2);
  not not_2 (not_2_out, A1);
  not not_3 (not_3_out, A0);
  and AND1 (AND1_out, not_3_out, not_2_out, not_1_out, I0);
  and AND2 (AND2_out, A0, not_2_out, not_1_out, I1);
  and AND3 (AND3_out, not_3_out, A1, not_1_out, I2);
  and AND4 (AND4_out, A0, A1, not_1_out, I3);
  and AND5 (AND5_out, not_3_out, not_2_out, A2, I4);
  and AND6 (AND6_out, A0, not_2_out, A2, I5);
  and AND7 (AND7_out, not_3_out, A1, A2, I6);
  and AND8 (AND8_out, A0, A1, A2, I7);
  or or_1 (S0, AND1_out, AND2_out, AND3_out, AND4_out, AND5_out, AND6_out, AND7_out, AND8_out);

  // Notes on the sheet:
  //   Multiplexador 8x3
endmodule

module FA (
  input  Carry_In,
  input  A0,
  input  B0,
  output Sum,
  output Carry_Out
);

  wire ha_compact_1_carry_out, ha_compact_1_sum, ha_compact_2_carry_out;

  HA_Compact ha_compact_1 (.A0(A0), .B0(B0), .Sum(ha_compact_1_sum), .Carry_Out(ha_compact_1_carry_out));
  HA_Compact ha_compact_2 (.A0(Carry_In), .B0(ha_compact_1_sum), .Sum(Sum), .Carry_Out(ha_compact_2_carry_out));
  or OR1 (Carry_Out, ha_compact_2_carry_out, ha_compact_1_carry_out);

  // Notes on the sheet:
  //   Ful Adder
endmodule

// HAs
module HA_Simple (
  input  A0,
  input  B0,
  output Sum,
  output Carry_Out
);

  wire not_1_out, OR1_out;

  or OR1 (OR1_out, A0, B0);
  not not_1 (not_1_out, Carry_Out);
  and AND1 (Carry_Out, A0, B0);
  and AND2 (Sum, OR1_out, not_1_out);

  // Notes on the sheet:
  //   Simple Half Adder
endmodule

// HAc
module HA_Compact (
  input  A0,
  input  B0,
  output Sum,
  output Carry_Out
);

  xor XOR1 (Sum, A0, B0);
  and AND1 (Carry_Out, A0, B0);

  // Notes on the sheet:
  //   Compact Half Adder
endmodule

module FD (
  input  Carry_In,
  input  A0,
  input  B0,
  output Diff,
  output Carry_Out
);

  wire hd_compact_1_carry_out, hd_compact_1_diff, hd_compact_2_carry_out;

  HD_Compact hd_compact_1 (.A0(A0), .B0(B0), .Diff(hd_compact_1_diff), .Carry_Out(hd_compact_1_carry_out));
  HD_Compact hd_compact_2 (.A0(Carry_In), .B0(hd_compact_1_diff), .Diff(Diff), .Carry_Out(hd_compact_2_carry_out));
  or OR1 (Carry_Out, hd_compact_2_carry_out, hd_compact_1_carry_out);

  // Notes on the sheet:
  //   Full Difference
endmodule

// HDc
module HD_Compact (
  input  A0,
  input  B0,
  output Diff,
  output Carry_Out
);

  wire not_1_out;

  not not_1 (not_1_out, A0);
  xor XOR1 (Diff, A0, B0);
  and AND1 (Carry_Out, B0, not_1_out);

  // Notes on the sheet:
  //   Compact Half Difference
endmodule

module EC (
  input  A0,
  input  B0,
  output S0
);

  xnor XNOR1 (S0, A0, B0);

  // Notes on the sheet:
  //   Equality Comparator
endmodule

module IC (
  input  A0,
  input  B0,
  output S0
);

  xor XOR1 (S0, A0, B0);

  // Notes on the sheet:
  //   Inequality Comparator
endmodule

module FFs (
  input  Set,
  input  Set_2,
  input  D,
  input  T,
  input  Preset,
  input  Preset_2,
  input  Set_3,
  input  Set_4,
  input  J,
  input  S,
  input  K,
  input  R,
  input  Preset_3,
  input  Preset_4,
  output Q,
  output Q_2,
  output Q_prime,
  output Q_prime_2,
  output Q_3,
  output Q_4,
  output Q_prime_3,
  output Q_prime_4
);

  wire Clock_2_out, Clock_3_out, clock_4_out, Clock_out;

  Clock Clock (.out(Clock_out));
  Clock Clock_2 (.out(Clock_2_out));
  D_Flip_Flop d_ff_1 (.clk(Clock_out), .D(D), .Q(Q), .Qn(Q_prime), .preset(Set), .reset(Preset));
  J_K_Flip_Flop j_k_ff_1 (.J(J), .clk(Clock_2_out), .K(K), .Q(Q_3), .Qn(Q_prime_3), .preset(Set_3), .reset(Preset_3));
  Clock Clock_3 (.out(Clock_3_out));
  Clock clock_4 (.out(clock_4_out));
  T_Flip_Flop t_ff_1 (.clk(Clock_3_out), .T(T), .Q(Q_2), .Qn(Q_prime_2), .preset(Set_2), .reset(Preset_2));
  S_R_Flip_Flop s_r_ff_1 (.S(S), .clk(clock_4_out), .R(R), .Q(Q_4), .Qn(Q_prime_4), .preset(Set_4), .reset(Preset_4));
endmodule

module Counters (
  input  in_1
);

  _7_Segment_Display u_7_segment_display_1 (.f(in_1), .a(in_1), .b(in_1), .e(in_1), .d(in_1), .c(in_1));  // open: g, dp
  _7_Segment_Display u_7_segment_display_2 (.f(in_1), .e(in_1));  // open: g, a, b, d, c, dp

  // Notes on the sheet:
  //   Counters - Contadores$$Organização:$    Ordem_Tipo_Quant.-de-Bits$$Onde: $    Ordem = crescente ou decrescente // up ou down$    Tipo = assíncrono, síncrono ou decádico // asinc, sinc ou decade$    Quant.-de-Bits = quantidade de bits do circuito 
endmodule

module DOWN_ASINC_4_bits (
  input  Clear
);

  wire j_k_ff_1_qn, j_k_ff_2_qn, j_k_ff_3_qn, j_k_ff_4_qn, Pulse_out;

  Button Pulse (.out(Pulse_out));
  // Probe on j_k_ff_1_qn
  J_K_Flip_Flop j_k_ff_1 (.J(1'b1), .clk(j_k_ff_2_qn), .K(1'b1), .Qn(j_k_ff_1_qn), .reset(Clear));  // open: Q, preset
  // Probe on j_k_ff_2_qn
  J_K_Flip_Flop j_k_ff_2 (.J(1'b1), .clk(j_k_ff_3_qn), .K(1'b1), .Qn(j_k_ff_2_qn), .reset(Clear));  // open: Q, preset
  J_K_Flip_Flop j_k_ff_3 (.J(1'b1), .clk(j_k_ff_4_qn), .K(1'b1), .Qn(j_k_ff_3_qn), .reset(Clear));  // open: Q, preset
  // Probe on j_k_ff_3_qn
  // Probe on j_k_ff_4_qn
  J_K_Flip_Flop j_k_ff_4 (.J(1'b1), .clk(Pulse_out), .K(1'b1), .Qn(j_k_ff_4_qn), .reset(Clear));  // open: Q, preset
endmodule

module UP_ASINC_4_bits (
  input  Clear
);

  wire j_k_ff_1_qn, j_k_ff_2_q, j_k_ff_2_qn, j_k_ff_3_q, j_k_ff_3_qn, j_k_ff_4_q, j_k_ff_4_qn, Pulse_out;

  Button Pulse (.out(Pulse_out));
  // Probe on j_k_ff_1_qn
  J_K_Flip_Flop j_k_ff_1 (.J(1'b1), .clk(j_k_ff_2_q), .K(1'b1), .Qn(j_k_ff_1_qn), .reset(Clear));  // open: Q, preset
  // Probe on j_k_ff_2_qn
  J_K_Flip_Flop j_k_ff_2 (
    .J(1'b1), .clk(j_k_ff_3_q), .K(1'b1), .Q(j_k_ff_2_q), .Qn(j_k_ff_2_qn), .reset(Clear));  // open: preset
  J_K_Flip_Flop j_k_ff_3 (
    .J(1'b1), .clk(j_k_ff_4_q), .K(1'b1), .Q(j_k_ff_3_q), .Qn(j_k_ff_3_qn), .reset(Clear));  // open: preset
  // Probe on j_k_ff_3_qn
  // Probe on j_k_ff_4_qn
  J_K_Flip_Flop j_k_ff_4 (
    .J(1'b1), .clk(Pulse_out), .K(1'b1), .Q(j_k_ff_4_q), .Qn(j_k_ff_4_qn), .reset(Clear));  // open: preset
endmodule

module DOWN_DECADE_4_bits (
);

  wire and_1_out, j_k_ff_1_q, j_k_ff_1_qn, j_k_ff_2_q, j_k_ff_2_qn, j_k_ff_3_q, j_k_ff_3_qn, j_k_ff_4_q,
       j_k_ff_4_qn, not_1_out, not_2_out, not_3_out, or_1_out, Pulse_out;

  Button Pulse (.out(Pulse_out));
  not not_1 (not_1_out, 1'b1);
  and and_1 (and_1_out, not_2_out, j_k_ff_2_qn, not_3_out, j_k_ff_4_qn);
  // Probe on j_k_ff_4_q
  J_K_Flip_Flop j_k_ff_1 (
    .J(1'b1), .clk(Pulse_out), .K(1'b1), .Q(j_k_ff_1_q), .Qn(j_k_ff_1_qn), .reset(or_1_out));  // open: preset
  or or_1 (or_1_out, not_1_out, and_1_out);
  not not_2 (not_2_out, j_k_ff_1_qn);
  not not_3 (not_3_out, j_k_ff_3_qn);
  // Probe on j_k_ff_3_q
  J_K_Flip_Flop j_k_ff_2 (
    .J(1'b1), .clk(j_k_ff_1_q), .K(1'b1), .Q(j_k_ff_2_q), .Qn(j_k_ff_2_qn), .reset(or_1_out));  // open: preset
  // Probe on j_k_ff_2_q
  J_K_Flip_Flop j_k_ff_3 (
    .J(1'b1), .clk(j_k_ff_2_q), .K(1'b1), .Q(j_k_ff_3_q), .Qn(j_k_ff_3_qn), .reset(or_1_out));  // open: preset
  // Probe on j_k_ff_1_q
  J_K_Flip_Flop j_k_ff_4 (
    .J(1'b1), .clk(j_k_ff_3_q), .K(1'b1), .Q(j_k_ff_4_q), .Qn(j_k_ff_4_qn), .reset(or_1_out));  // open: preset

  // Notes on the sheet:
  //   15 to 5
endmodule

module UP_DECADE_4_bits (
  input  Clear
);

  wire j_k_ff_1_q, j_k_ff_1_qn, j_k_ff_2_q, j_k_ff_2_qn, j_k_ff_3_q, j_k_ff_3_qn, j_k_ff_4_q, nand_1_out,
       nand_2_out, not_1_out, not_2_out, Pulse_out;

  Button Pulse (.out(Pulse_out));
  nand nand_1 (nand_1_out, Clear, nand_2_out);
  nand nand_2 (nand_2_out, not_1_out, j_k_ff_2_q, not_2_out, j_k_ff_4_q);
  // Probe on j_k_ff_4_q
  J_K_Flip_Flop j_k_ff_1 (
    .J(1'b1), .clk(Pulse_out), .K(1'b1), .Q(j_k_ff_1_q), .Qn(j_k_ff_1_qn), .reset(nand_1_out));  // open: preset
  not not_1 (not_1_out, j_k_ff_1_q);
  not not_2 (not_2_out, j_k_ff_3_q);
  // Probe on j_k_ff_3_q
  J_K_Flip_Flop j_k_ff_2 (
    .J(1'b1), .clk(j_k_ff_1_qn), .K(1'b1), .Q(j_k_ff_2_q), .Qn(j_k_ff_2_qn), .reset(nand_1_out));  // open: preset
  // Probe on j_k_ff_2_q
  J_K_Flip_Flop j_k_ff_3 (
    .J(1'b1), .clk(j_k_ff_2_qn), .K(1'b1), .Q(j_k_ff_3_q), .Qn(j_k_ff_3_qn), .reset(nand_1_out));  // open: preset
  // Probe on j_k_ff_1_q
  J_K_Flip_Flop j_k_ff_4 (
    .J(1'b1), .clk(j_k_ff_3_qn), .K(1'b1), .Q(j_k_ff_4_q), .reset(nand_1_out));  // open: Qn, preset

  // Notes on the sheet:
  //   0 to 10
endmodule

module DOWN_SINC_4_bits (
  input  Clear
);

  wire and_1_out, and_2_out, and_3_out, Clock_out, j_k_ff_1_q, j_k_ff_1_qn, j_k_ff_2_q, j_k_ff_2_qn,
       j_k_ff_3_q, j_k_ff_3_qn, j_k_ff_4_q, not_1_out;

  Clock Clock (.out(Clock_out));
  // Probe on j_k_ff_4_q
  J_K_Flip_Flop j_k_ff_1 (
    .J(1'b1), .clk(Clock_out), .K(1'b1), .Q(j_k_ff_1_q), .Qn(j_k_ff_1_qn), .reset(Clear));  // open: preset
  and and_1 (and_1_out, j_k_ff_1_qn, not_1_out);
  not not_1 (not_1_out, Clear);
  // Probe on j_k_ff_3_q
  J_K_Flip_Flop j_k_ff_2 (
    .J(and_1_out), .clk(Clock_out), .K(and_1_out), .Q(j_k_ff_2_q), .Qn(j_k_ff_2_qn), .reset(Clear));  // open: preset
  // Probe on j_k_ff_2_q
  and and_2 (and_2_out, j_k_ff_2_qn, and_1_out);
  J_K_Flip_Flop j_k_ff_3 (
    .J(and_2_out), .clk(Clock_out), .K(and_2_out), .Q(j_k_ff_3_q), .Qn(j_k_ff_3_qn), .reset(Clear));  // open: preset
  and and_3 (and_3_out, j_k_ff_3_qn, and_2_out);
  // Probe on j_k_ff_1_q
  J_K_Flip_Flop j_k_ff_4 (
    .J(and_3_out), .clk(Clock_out), .K(and_3_out), .Q(j_k_ff_4_q), .reset(Clear));  // open: Qn, preset
endmodule

module UP_SINC_4_bits (
  input  Clear
);

  wire and_1_out, and_2_out, Clock_out, j_k_ff_1_q, j_k_ff_2_q, j_k_ff_3_q, j_k_ff_4_q;

  Clock Clock (.out(Clock_out));
  // Probe on j_k_ff_4_q
  J_K_Flip_Flop j_k_ff_1 (.J(1'b1), .clk(Clock_out), .K(1'b1), .Q(j_k_ff_1_q), .reset(Clear));  // open: Qn, preset
  // Probe on j_k_ff_3_q
  J_K_Flip_Flop j_k_ff_2 (
    .J(j_k_ff_1_q), .clk(Clock_out), .K(j_k_ff_1_q), .Q(j_k_ff_2_q), .reset(Clear));  // open: Qn, preset
  // Probe on j_k_ff_2_q
  and and_1 (and_1_out, j_k_ff_2_q, j_k_ff_1_q);
  J_K_Flip_Flop j_k_ff_3 (
    .J(and_1_out), .clk(Clock_out), .K(and_1_out), .Q(j_k_ff_3_q), .reset(Clear));  // open: Qn, preset
  and and_2 (and_2_out, j_k_ff_3_q, j_k_ff_2_q, j_k_ff_1_q);
  // Probe on j_k_ff_1_q
  J_K_Flip_Flop j_k_ff_4 (
    .J(and_2_out), .clk(Clock_out), .K(and_2_out), .Q(j_k_ff_4_q), .reset(Clear));  // open: Qn, preset
endmodule

module RING_3_bits (
  input  Input,
  input  Clear
);

  wire Clock_out, d_ff_1_q, d_ff_2_q, d_ff_3_q, or_1_out;

  Clock Clock (.out(Clock_out));
  or or_1 (or_1_out, d_ff_3_q, Input);
  D_Flip_Flop d_ff_1 (.clk(Clock_out), .D(or_1_out), .Q(d_ff_1_q), .reset(Clear));  // open: Qn, preset
  D_Flip_Flop d_ff_2 (.clk(Clock_out), .D(d_ff_1_q), .Q(d_ff_2_q), .reset(Clear));  // open: Qn, preset
  // Probe on d_ff_1_q
  // Probe on d_ff_2_q
  // Probe on d_ff_3_q
  D_Flip_Flop d_ff_3 (.clk(Clock_out), .D(d_ff_2_q), .Q(d_ff_3_q), .reset(Clear));  // open: Qn, preset
endmodule

module TWISTED_RING_3_bits (
  input  Input,
  input  Clear
);

  wire Clock_out, d_ff_1_q, d_ff_2_q, d_ff_3_q, d_ff_3_qn, or_1_out;

  Clock Clock (.out(Clock_out));
  or or_1 (or_1_out, Input, d_ff_3_qn);
  D_Flip_Flop d_ff_1 (.clk(Clock_out), .D(or_1_out), .Q(d_ff_1_q), .reset(Clear));  // open: Qn, preset
  D_Flip_Flop d_ff_2 (.clk(Clock_out), .D(d_ff_1_q), .Q(d_ff_2_q), .reset(Clear));  // open: Qn, preset
  // Probe on d_ff_1_q
  // Probe on d_ff_2_q
  // Probe on d_ff_3_q
  D_Flip_Flop d_ff_3 (.clk(Clock_out), .D(d_ff_2_q), .Q(d_ff_3_q), .Qn(d_ff_3_qn), .reset(Clear));  // open: preset
endmodule

module BASE_X_3_bits (
  input  Clear
);

  wire and_1_out, not_1_out, or_1_out, Pulse_out, t_ff_1_q, t_ff_2_q, t_ff_2_qn, t_ff_3_q, t_ff_3_qn;

  Button Pulse (.out(Pulse_out));
  or or_1 (or_1_out, Clear, and_1_out);
  // Probe on t_ff_1_q
  T_Flip_Flop t_ff_1 (.clk(t_ff_2_qn), .T(t_ff_2_qn), .Q(t_ff_1_q), .reset(or_1_out));  // open: Qn, preset
  not not_1 (not_1_out, t_ff_2_q);
  and and_1 (and_1_out, t_ff_1_q, not_1_out, t_ff_3_q);
  // Probe on t_ff_2_q
  T_Flip_Flop t_ff_2 (.clk(t_ff_3_qn), .T(t_ff_3_qn), .Q(t_ff_2_q), .Qn(t_ff_2_qn), .reset(or_1_out));  // open: preset
  // Probe on t_ff_3_q
  T_Flip_Flop t_ff_3 (.clk(Pulse_out), .T(Pulse_out), .Q(t_ff_3_q), .Qn(t_ff_3_qn), .reset(or_1_out));  // open: preset

  // Notes on the sheet:
  //   0 to 5
endmodule

module SHIFT_LEFT_4_bits (
  input  Data,
  input  Clear
);

  wire Clock_out, d_ff_1_q, d_ff_2_q, d_ff_3_q, d_ff_4_q;

  Clock Clock (.out(Clock_out));
  // Probe on d_ff_1_q
  D_Flip_Flop d_ff_1 (.clk(Clock_out), .D(d_ff_2_q), .Q(d_ff_1_q), .reset(Clear));  // open: Qn, preset
  // Probe on d_ff_2_q
  D_Flip_Flop d_ff_2 (.clk(Clock_out), .D(d_ff_3_q), .Q(d_ff_2_q), .reset(Clear));  // open: Qn, preset
  D_Flip_Flop d_ff_3 (.clk(Clock_out), .D(d_ff_4_q), .Q(d_ff_3_q), .reset(Clear));  // open: Qn, preset
  // Probe on d_ff_3_q
  // Probe on d_ff_4_q
  D_Flip_Flop d_ff_4 (.clk(Clock_out), .D(Data), .Q(d_ff_4_q), .reset(Clear));  // open: Qn, preset
endmodule

module SHIFT_RIGTH_4_bits (
  input  Data,
  input  Clear
);

  wire Clock_out, d_ff_1_q, d_ff_2_q, d_ff_3_q, d_ff_4_q;

  Clock Clock (.out(Clock_out));
  // Probe on d_ff_1_q
  D_Flip_Flop d_ff_1 (.clk(Clock_out), .D(Data), .Q(d_ff_1_q), .reset(Clear));  // open: Qn, preset
  // Probe on d_ff_2_q
  D_Flip_Flop d_ff_2 (.clk(Clock_out), .D(d_ff_1_q), .Q(d_ff_2_q), .reset(Clear));  // open: Qn, preset
  D_Flip_Flop d_ff_3 (.clk(Clock_out), .D(d_ff_2_q), .Q(d_ff_3_q), .reset(Clear));  // open: Qn, preset
  // Probe on d_ff_3_q
  // Probe on d_ff_4_q
  D_Flip_Flop d_ff_4 (.clk(Clock_out), .D(d_ff_3_q), .Q(d_ff_4_q), .reset(Clear));  // open: Qn, preset
endmodule

module PARELLEL_IN_SERIAL_OUT_4_bits (
  input  I3,
  input  I2,
  input  I1,
  input  I1_2,
  input  Load,
  input  Clear
);

  wire and_1_out, and_2_out, and_3_out, and_4_out, Clock_out, d_ff_1_q, d_ff_2_q, d_ff_3_q, d_ff_4_q;

  Clock Clock (.out(Clock_out));
  and and_1 (and_1_out, Load, I3);
  D_Flip_Flop d_ff_1 (.clk(Clock_out), .D(1'b0), .Q(d_ff_1_q), .preset(and_1_out), .reset(Clear));  // open: Qn
  // Probe on d_ff_1_q
  and and_2 (and_2_out, Load, I2);
  D_Flip_Flop d_ff_2 (.clk(Clock_out), .D(d_ff_1_q), .Q(d_ff_2_q), .preset(and_2_out), .reset(Clear));  // open: Qn
  // Probe on d_ff_2_q
  and and_3 (and_3_out, Load, I1);
  D_Flip_Flop d_ff_3 (.clk(Clock_out), .D(d_ff_2_q), .Q(d_ff_3_q), .preset(and_3_out), .reset(Clear));  // open: Qn
  and and_4 (and_4_out, Load, I1_2);
  // Probe on d_ff_3_q
  D_Flip_Flop d_ff_4 (.clk(Clock_out), .D(d_ff_3_q), .Q(d_ff_4_q), .preset(and_4_out), .reset(Clear));  // open: Qn
  // Probe on d_ff_4_q
endmodule

module ROTATE_RIGHT_4_bits (
  input  Data,
  input  Clear
);

  wire Clock_out, d_ff_1_q, d_ff_2_q, d_ff_3_q, d_ff_4_q, or_1_out;

  Clock Clock (.out(Clock_out));
  or or_1 (or_1_out, d_ff_4_q, Data);
  // Probe on d_ff_1_q
  D_Flip_Flop d_ff_1 (.clk(Clock_out), .D(or_1_out), .Q(d_ff_1_q), .reset(Clear));  // open: Qn, preset
  // Probe on d_ff_2_q
  D_Flip_Flop d_ff_2 (.clk(Clock_out), .D(d_ff_1_q), .Q(d_ff_2_q), .reset(Clear));  // open: Qn, preset
  D_Flip_Flop d_ff_3 (.clk(Clock_out), .D(d_ff_2_q), .Q(d_ff_3_q), .reset(Clear));  // open: Qn, preset
  // Probe on d_ff_3_q
  // Probe on d_ff_4_q
  D_Flip_Flop d_ff_4 (.clk(Clock_out), .D(d_ff_3_q), .Q(d_ff_4_q), .reset(Clear));  // open: Qn, preset
endmodule

module ROTATE_LEFT_4_bits (
  input  Data,
  input  Clear
);

  wire Clock_out, d_ff_1_q, d_ff_2_q, d_ff_3_q, d_ff_4_q, or_1_out;

  Clock Clock (.out(Clock_out));
  or or_1 (or_1_out, d_ff_1_q, Data);
  // Probe on d_ff_1_q
  D_Flip_Flop d_ff_1 (.clk(Clock_out), .D(d_ff_2_q), .Q(d_ff_1_q), .reset(Clear));  // open: Qn, preset
  // Probe on d_ff_2_q
  D_Flip_Flop d_ff_2 (.clk(Clock_out), .D(d_ff_3_q), .Q(d_ff_2_q), .reset(Clear));  // open: Qn, preset
  // Probe on d_ff_3_q
  D_Flip_Flop d_ff_3 (.clk(Clock_out), .D(d_ff_4_q), .Q(d_ff_3_q), .reset(Clear));  // open: Qn, preset
  D_Flip_Flop d_ff_4 (.clk(Clock_out), .D(or_1_out), .Q(d_ff_4_q), .reset(Clear));  // open: Qn, preset
  // Probe on d_ff_4_q
endmodule

module REGISTER_4_bits (
  input  I3,
  input  I2,
  input  I1,
  input  I0,
  input  Rigth_Bit,
  input  Left_Bit,
  input  [1:0] Mode,
  input  Clear,
  output O3,
  output O2,
  output O1,
  output O0
);

  wire Clock_out, multiplexer_1_out, multiplexer_2_out, multiplexer_3_out, multiplexer_4_out;

  Clock Clock (.out(Clock_out));
  Multiplexer #(.select(2), .enable("false")) multiplexer_1 (
    .in0(O3), .in1(Rigth_Bit), .in2(O2), .in3(I3), .out(multiplexer_1_out), .sel(Mode));
  D_Flip_Flop d_ff_1 (.clk(Clock_out), .D(multiplexer_1_out), .Q(O3), .reset(Clear));  // open: Qn, preset
  Multiplexer #(.select(2), .enable("false")) multiplexer_2 (
    .in0(O2), .in1(O3), .in2(O1), .in3(I2), .out(multiplexer_2_out), .sel(Mode));
  D_Flip_Flop d_ff_2 (.clk(Clock_out), .D(multiplexer_2_out), .Q(O2), .reset(Clear));  // open: Qn, preset
  Multiplexer #(.select(2), .enable("false")) multiplexer_3 (
    .in0(O1), .in1(O2), .in2(O0), .in3(I1), .out(multiplexer_3_out), .sel(Mode));
  Multiplexer #(.select(2), .enable("false")) multiplexer_4 (
    .in0(O0), .in1(O1), .in2(Left_Bit), .in3(I0), .out(multiplexer_4_out), .sel(Mode));
  D_Flip_Flop d_ff_3 (.clk(Clock_out), .D(multiplexer_3_out), .Q(O1), .reset(Clear));  // open: Qn, preset
  D_Flip_Flop d_ff_4 (.clk(Clock_out), .D(multiplexer_4_out), .Q(O0), .reset(Clear));  // open: Qn, preset
endmodule
