// Logisim project Guia_0501.circ as structural Verilog: 1 circuit, main circuit main
// not_a
module main (
  input  a,
  input  b,
  output s
);

  wire NOR1_out;

  nor NOR1 (NOR1_out, a, a);
  nor NOR2 (s, NOR1_out, b);
endmodule
