// Logisim project Guia_0503.circ as structural Verilog: 1 circuit, main circuit main
module main (
  input  a,
  input  b,
  output s
);

  wire NOR1_out, NOR2_out;

  nor NOR1 (NOR1_out, a, a);
  nor NOR2 (NOR2_out, NOR1_out, b);
  nor NOR3 (s, NOR2_out, NOR2_out);
endmodule
