// Logisim project Guia_0505.circ as structural Verilog: 1 circuit, main circuit main
module main (
  input  a,
  input  b,
  output s
);

  wire NOR1_out, NOR2_out, NOR3_out;

  nor NOR1 (NOR1_out, a, a);
  nor NOR2 (NOR2_out, b, b);
  nor NOR3 (NOR3_out, NOR1_out, NOR2_out);
  nor NOR4 (s, NOR3_out, NOR3_out);
endmodule
