// Logisim project Guia_0506.circ as structural Verilog: 1 circuit, main circuit main
module main (
  input  a,
  input  b,
  output s
);

  wire NAND1_out;

  nand NAND1 (NAND1_out, a, b);
  nand NAND2 (s, NAND1_out, NAND1_out);
endmodule
