// Logisim project Guia_0507.circ as structural Verilog: 1 circuit, main circuit main
module main (
  input  a,
  input  b,
  output s
);

  wire NOR1_out;

  nor NOR1 (NOR1_out, a, b);
  nor NOR2 (s, NOR1_out, NOR1_out);
endmodule
