// Logisim project Guia_0508.circ as structural Verilog: 1 circuit, main circuit main
module main (
  input  a,
  input  b,
  output s
);

  wire NAND1_out, NAND2_out;

  nand NAND1 (NAND1_out, a, a);
  nand NAND2 (NAND2_out, b, b);
  nand NAND3 (s, NAND1_out, NAND2_out);
endmodule
