// Logisim project Guia_0605.circ as structural Verilog: 1 circuit, main circuit main
module main (
  input  x,
  input  y,
  input  z,
  output s
);

  wire AND_2_out, AND_out, not_1_out, not_2_out;

  and AND (AND_out, x, not_1_out);
  not not_1 (not_1_out, z);
  and AND_2 (AND_2_out, x, not_2_out);
  not not_2 (not_2_out, y);
  or OR (s, AND_out, AND_2_out);

  // Notes on the sheet:
  //   Guia_0605
  //   Vinícius Miranda de Araújo - 812839
  //   Expressão: f(x,y,z) = (x.z')+(x.y')
endmodule
