// Logisim project Guia_0606.circ as structural Verilog: 1 circuit, main circuit main
module main (
  input  X,
  input  Y,
  input  W,
  input  Z,
  output S
);

  wire AND1_out, not_1_out, not_2_out, not_3_out, not_4_out, OR1_out, OR2_out, OR3_out, OR4_out;

  or OR1 (OR1_out, X, W);
  or OR2 (OR2_out, X, not_1_out);
  not not_1 (not_1_out, W);
  not not_2 (not_2_out, Y);
  or OR3 (OR3_out, not_2_out, not_3_out);
  not not_3 (not_3_out, W);
  not not_4 (not_4_out, Z);
  and AND1 (AND1_out, OR1_out, OR2_out);
  or OR4 (OR4_out, OR3_out, not_4_out);
  and AND2 (S, AND1_out, OR4_out);

  // Notes on the sheet:
  //   Guia_0606
  //   Vinícius Miranda de Araújo - 812839
  //   Expressão: f(X,Y,W,Z) = (X+W) . (X+W') . (Y'+W'+Z')
endmodule
