// Logisim project Guia_0607.circ as structural Verilog: 1 circuit, main circuit main
module main (
  input  X,
  input  Y,
  input  Z,
  output S
);

  wire not_1_out, not_2_out, OR1_out, OR2_out, OR3_out;

  not not_1 (not_1_out, Y);
  not not_2 (not_2_out, X);
  or OR1 (OR1_out, X, not_1_out);
  or OR2 (OR2_out, not_2_out, Y);
  or OR3 (OR3_out, OR2_out, Z);
  and AND1 (S, OR1_out, OR3_out);

  // Notes on the sheet:
  //   Vinícius Miranda de Araújo - 812839
  //   Guia_0607 - Extra
  //   Expressão: f(X,Y,Z) = (X+Y') . (X'+Y+Z)
endmodule
