// Logisim project Guia_0608.circ as structural Verilog: 1 circuit, main circuit main
module main (
  input  w,
  input  x,
  input  y,
  input  z,
  output s
);

  wire AND1_out, AND2_out, AND3_out, AND4_out, AND5_out, AND6_out, AND7_out, AND8_out, AND9_out, AND10_out,
       AND11_out, AND12_out, not_1_out, not_2_out, not_3_out, not_4_out, not_5_out, not_6_out, not_7_out,
       OR1_out, OR2_out;

  and AND1 (AND1_out, w, x);
  and AND2 (AND2_out, y, z);
  and AND4 (AND4_out, w, x);
  not not_1 (not_1_out, y);
  and AND5 (AND5_out, not_1_out, not_2_out);
  not not_2 (not_2_out, z);
  and AND7 (AND7_out, w, not_3_out);
  not not_3 (not_3_out, x);
  not not_4 (not_4_out, y);
  and AND8 (AND8_out, not_4_out, z);
  not not_5 (not_5_out, w);
  and AND10 (AND10_out, not_5_out, not_6_out);
  not not_6 (not_6_out, x);
  and AND11 (AND11_out, y, not_7_out);
  not not_7 (not_7_out, z);
  and AND3 (AND3_out, AND1_out, AND2_out);
  and AND6 (AND6_out, AND4_out, AND5_out);
  and AND9 (AND9_out, AND7_out, AND8_out);
  and AND12 (AND12_out, AND10_out, AND11_out);
  or OR1 (OR1_out, AND3_out, AND6_out);
  or OR2 (OR2_out, AND9_out, AND12_out);
  or OR3 (s, OR1_out, OR2_out);

  // Notes on the sheet:
  //   Guia_0608 - Extra
  //   Vinícius Miranda de Araújo - 812839
  //   Expressão: f(w,x,y,z) = (w.x.y.z) + (w.x.y'.z') + (w.x'.y'.z) + (w'.x'.y.z')
endmodule
