// Logisim project Guia_0701.circ as structural Verilog: 1 circuit, main circuit main
module main (
  input  x,
  input  y,
  input  s,
  output z
);

  wire AND_out, NAND_out;

  and AND (AND_out, x, y);
  nand NAND (NAND_out, x, y);
  MUX_2x1 mux_2x1_1 (.x(AND_out), .y(NAND_out), .out_4(z), .a1(s));

  // Notes on the sheet:
  //   Guia_0701
  //   Vinícius Miranda de Araújo - 812839
endmodule
