// Logisim project Guia_0702.circ as structural Verilog: 1 circuit, main circuit main
module main (
  input  x,
  input  y,
  input  s,
  output z
);

  wire NOR_out, OR_out;

  or OR (OR_out, x, y);
  nor NOR (NOR_out, x, y);
  MUX_2x1 mux_2x1_1 (.x(OR_out), .y(NOR_out), .out_4(z), .a1(s));

  // Notes on the sheet:
  //   Guia_0702
  //   Vinícius Miranda de Araújo - 812839
endmodule
