// Logisim project Guia_0703.circ as structural Verilog: 1 circuit, main circuit main
module main (
  input  x,
  input  y,
  input  s1,
  input  S3,
  input  s2,
  output z
);

  wire AND_out, mux_2x1_1_out_4, mux_2x1_2_out_4, NAND_out, NOR_out, OR_out;

  and AND (AND_out, x, y);
  nand NAND (NAND_out, x, y);
  or OR (OR_out, x, y);
  nor NOR (NOR_out, x, y);
  MUX_2x1 mux_2x1_1 (.x(AND_out), .y(NAND_out), .out_4(mux_2x1_1_out_4), .a1(s1));
  MUX_2x1 mux_2x1_2 (.x(OR_out), .y(NOR_out), .out_4(mux_2x1_2_out_4), .a1(s2));
  MUX_2x1 mux_2x1_3 (.x(mux_2x1_1_out_4), .y(mux_2x1_2_out_4), .out_4(z), .a1(S3));

  // Notes on the sheet:
  //   Guia_0703
  //   Vinícius Miranda de Araújo - 812839
endmodule
