// Logisim project Guia_0704.circ as structural Verilog: 1 circuit, main circuit main
module main (
  input  x,
  input  y,
  input  in_3,
  input  in_4,
  output z
);

  wire NOR_out, OR_out, XNOR_out, XOR_out;

  or OR (OR_out, x, y);
  nor NOR (NOR_out, x, y);
  xor XOR (XOR_out, x, y);
  xnor XNOR (XNOR_out, x, y);
  MUX_4x2 mux_4x2_1 (.i1(OR_out), .i2(NOR_out), .i4(XNOR_out), .s(z), .a1(in_3), .a0(in_4), .i3(XOR_out));

  // Notes on the sheet:
  //   Guia_0704
  //   Vinícius Miranda de Araújo - 812839
endmodule
