// Logisim project Guia_0705.circ as structural Verilog: 1 circuit, main circuit main
module main (
  input  x,
  input  y,
  input  in_3,
  input  in_4,
  input  in_5,
  output z
);

  wire AND_out, NAND_out, NOR_out, NOT_X_out, NOT_Y_out, OR_out, XNOR_out, XOR_out;

  not NOT_X (NOT_X_out, x);
  not NOT_Y (NOT_Y_out, y);
  and AND (AND_out, x, y);
  nand NAND (NAND_out, x, y);
  or OR (OR_out, x, y);
  nor NOR (NOR_out, x, y);
  xor XOR (XOR_out, x, y);
  xnor XNOR (XNOR_out, x, y);
  MUX_8x3 mux_8x3_1 (
    .i0(NOT_X_out), .i1(NOT_Y_out), .i2(AND_out), .i3(NAND_out), .i4(OR_out), .i5(NOR_out), .i6(XOR_out),
    .i7(XNOR_out), .s(z), .a2(in_3), .a1(in_4), .a0(in_5));

  // Notes on the sheet:
  //   Guia_0705
  //   Vinícius Miranda de Araújo - 812839
endmodule
