// Logisim project Guia_0801.circ as structural Verilog: 1 circuit, main circuit main
module main (
  input  b4,
  input  a4,
  input  b3,
  input  a3,
  input  b2,
  input  a2,
  input  b1,
  input  a1,
  input  b0,
  input  a0,
  output s05,
  output s04,
  output s03,
  output s02,
  output s01,
  output s00
);

  wire fa_2_carryout, fa_3_carryout, fa_4_carryout, fa_5_carryout;

  FA fa_1 (.carryIn(fa_2_carryout), .x(a4), .y(b4), .sum(s04), .carryOut(s05));
  FA fa_2 (.carryIn(fa_3_carryout), .x(a3), .y(b3), .sum(s03), .carryOut(fa_2_carryout));
  FA fa_3 (.carryIn(fa_4_carryout), .x(a2), .y(b2), .sum(s02), .carryOut(fa_3_carryout));
  FA fa_4 (.carryIn(fa_5_carryout), .x(a1), .y(b1), .sum(s01), .carryOut(fa_4_carryout));
  FA fa_5 (.carryIn(1'b0), .x(a0), .y(b0), .sum(s00), .carryOut(fa_5_carryout));

  // Notes on the sheet:
  //   Vinicius Miranda de Araujo - 812839$Guia_0801$Somador Completo de 5 bits
  //   "vai-um" = 0
endmodule
