// Logisim project Guia_0802.circ as structural Verilog: 1 circuit, main circuit main
module main (
  input  b5,
  input  a5,
  input  b4,
  input  a4,
  input  b3,
  input  a3,
  input  b2,
  input  a2,
  input  b1,
  input  a1,
  input  b0,
  input  a0,
  output s06,
  output s05,
  output s04,
  output s03,
  output s02,
  output s01,
  output s00
);

  wire fd_2_carryout, fd_3_carryout, fd_4_carryout, fd_5_carryout, fd_6_carryout;

  FD fd_1 (.carryIn(fd_2_carryout), .x(a5), .y(b5), .diff(s05), .carryOut(s06));
  FD fd_2 (.carryIn(fd_3_carryout), .x(a4), .y(b4), .diff(s04), .carryOut(fd_2_carryout));
  FD fd_3 (.carryIn(fd_4_carryout), .x(a3), .y(b3), .diff(s03), .carryOut(fd_3_carryout));
  FD fd_4 (.carryIn(fd_5_carryout), .x(a2), .y(b2), .diff(s02), .carryOut(fd_4_carryout));
  FD fd_5 (.carryIn(fd_6_carryout), .x(a1), .y(b1), .diff(s01), .carryOut(fd_5_carryout));
  FD fd_6 (.carryIn(1'b0), .x(a0), .y(b0), .diff(s00), .carryOut(fd_6_carryout));

  // Notes on the sheet:
  //   Vinicius Miranda de Araujo - 812839$Guia_0802$Subtrator Completo de 6 bits
  //   "vem-um" = 0
endmodule
