// Logisim project Guia_0803.circ as structural Verilog: 1 circuit, main circuit main
module main (
  input  b5,
  input  a5,
  input  b4,
  input  a4,
  input  b3,
  input  a3,
  input  b2,
  input  a2,
  input  b1,
  input  a1,
  input  b0,
  input  a0,
  output s05,
  output s04,
  output s03,
  output s02,
  output s01,
  output s00
);

  EC ec_1 (.x(a5), .y(b5), .s(s05));
  EC ec_2 (.x(a4), .y(b4), .s(s04));
  EC ec_3 (.x(a3), .y(b3), .s(s03));
  EC ec_4 (.x(a2), .y(b2), .s(s02));
  EC ec_5 (.x(a1), .y(b1), .s(s01));
  EC ec_6 (.x(a0), .y(b0), .s(s00));

  // Notes on the sheet:
  //   Vinicius Miranda de Araujo - 812839$Guia_0803$Compardor de Igualdade de 6 bits
endmodule
