// Logisim project Guia_0805.circ as structural Verilog: 2 circuits, main circuit main
module main (
  input  x4,
  input  x3,
  input  x2,
  input  x1,
  input  x0,
  output carryOut,
  output s4,
  output s3,
  output s2,
  output s1,
  output s0
);

  wire c1_1_out_6, c1_1_out_7, c1_1_out_8, c1_1_out_9, c1_1_out_10, fa_2_carryout, fa_3_carryout,
       fa_4_carryout, fa_5_carryout;

  FA fa_1 (.carryIn(fa_2_carryout), .x(c1_1_out_6), .y(1'b0), .sum(s4), .carryOut(carryOut));
  C1 c1_1 (
    .in_1(x4), .in_2(x3), .in_3(x2), .in_4(x1), .in_5(x0), .out_6(c1_1_out_6), .out_7(c1_1_out_7),
    .out_8(c1_1_out_8), .out_9(c1_1_out_9), .out_10(c1_1_out_10));
  FA fa_2 (.carryIn(fa_3_carryout), .x(c1_1_out_7), .y(1'b0), .sum(s3), .carryOut(fa_2_carryout));
  FA fa_3 (.carryIn(fa_4_carryout), .x(c1_1_out_8), .y(1'b0), .sum(s2), .carryOut(fa_3_carryout));
  FA fa_4 (.carryIn(fa_5_carryout), .x(c1_1_out_9), .y(1'b0), .sum(s1), .carryOut(fa_4_carryout));
  FA fa_5 (.carryIn(1'b0), .x(c1_1_out_10), .y(1'b1), .sum(s0), .carryOut(fa_5_carryout));

  // Notes on the sheet:
  //   Vinicius Miranda de Araujo - 812839$Guia_0805$Two's Complement for 5 bits
  //   carryIn
endmodule

module C1 (
  input  in_1,
  input  in_2,
  input  in_3,
  input  in_4,
  input  in_5,
  output out_6,
  output out_7,
  output out_8,
  output out_9,
  output out_10
);

  not not_1 (out_6, in_1);
  not not_2 (out_7, in_2);
  not not_3 (out_8, in_3);
  not not_4 (out_10, in_5);
  not not_5 (out_9, in_4);

  // Notes on the sheet:
  //   One's complement for 5 bits
endmodule
