// Logisim project libshow.circ as structural Verilog: 11 circuits, main circuit main
module main (
);

  Multiplexer #(.select(3), .enable("false")) multiplexer_1 ();  // open: in0, in1, in2, in3, in4, in5, in6, in7, out, sel
endmodule

// MUX
module MUX_2x1 (
  input  x,
  input  y,
  input  a1,
  output out_4
);

  wire AND1_out, AND2_out, not_1_out;

  and AND1 (AND1_out, x, not_1_out);
  not not_1 (not_1_out, a1);
  and AND2 (AND2_out, y, a1);
  or OR1 (out_4, AND1_out, AND2_out);

  // Notes on the sheet:
  //   Multiplexador 2x1
endmodule

// MUX
module MUX_4x2 (
  input  a1,
  input  a0,
  input  i1,
  input  i2,
  input  i3,
  input  i4,
  output s
);

  wire AND1_out, AND2_out, AND3_out, AND4_out, not_1_out, not_2_out;

  not not_1 (not_1_out, a1);
  not not_2 (not_2_out, a0);
  and AND1 (AND1_out, not_2_out, not_1_out, i1);
  and AND2 (AND2_out, a0, not_1_out, i2);
  and AND3 (AND3_out, not_2_out, a1, i3);
  and AND4 (AND4_out, a0, a1, i4);
  or OR1 (s, AND1_out, AND2_out, AND3_out, AND4_out);

  // Notes on the sheet:
  //   Multiplexador 4x2
endmodule

// MUX
module MUX_8x3 (
  input  a2,
  input  a1,
  input  a0,
  input  i0,
  input  i1,
  input  i2,
  input  i3,
  input  i4,
  input  i5,
  input  i6,
  input  i7,
  output s
);

  wire AND1_out, AND2_out, AND3_out, AND4_out, AND5_out, AND6_out, AND7_out, AND8_out, not_1_out, not_2_out,
       not_3_out;

  not not_1 (not_1_out, a1);
  not not_2 (not_2_out, a2);
  not not_3 (not_3_out, a0);
  and AND1 (AND1_out, not_3_out, not_1_out, not_2_out, i0);
  and AND2 (AND2_out, a0, not_1_out, not_2_out, i1);
  and AND3 (AND3_out, not_3_out, a1, not_2_out, i2);
  and AND4 (AND4_out, a0, a1, not_2_out, i3);
  and AND5 (AND5_out, not_3_out, not_1_out, a2, i4);
  and AND6 (AND6_out, a0, not_1_out, a2, i5);
  and AND7 (AND7_out, not_3_out, a1, a2, i6);
  and AND8 (AND8_out, a0, a1, a2, i7);
  or or_1 (s, AND1_out, AND2_out, AND3_out, AND4_out, AND5_out, AND6_out, AND7_out, AND8_out);

  // Notes on the sheet:
  //   Multiplexador 8x3
endmodule

module FA (
  input  carryIn,
  input  x,
  input  y,
  output sum,
  output carryOut
);

  wire ha_compact_1_carry, ha_compact_1_sum, ha_compact_2_carry;

  HA_Compact ha_compact_1 (.x(x), .y(y), .sum(ha_compact_1_sum), .carry(ha_compact_1_carry));
  HA_Compact ha_compact_2 (.x(carryIn), .y(ha_compact_1_sum), .sum(sum), .carry(ha_compact_2_carry));
  or OR1 (carryOut, ha_compact_2_carry, ha_compact_1_carry);

  // Notes on the sheet:
  //   Ful Adder
endmodule

// HAs
module HA_Simple (
  input  x,
  input  y,
  output sum,
  output carry
);

  wire not_1_out, OR1_out;

  or OR1 (OR1_out, x, y);
  not not_1 (not_1_out, carry);
  and AND1 (carry, x, y);
  and AND2 (sum, OR1_out, not_1_out);

  // Notes on the sheet:
  //   Simple Half Adder
endmodule

// HAc
module HA_Compact (
  input  x,
  input  y,
  output sum,
  output carry
);

  xor XOR1 (sum, x, y);
  and AND1 (carry, x, y);

  // Notes on the sheet:
  //   Compact Half Adder
endmodule

module FD (
  input  carryIn,
  input  x,
  input  y,
  output diff,
  output carryOut
);

  wire hd_compact_1_carr, hd_compact_1_diff, hd_compact_2_carr;

  HD_Compact hd_compact_1 (.x(x), .y(y), .diff(hd_compact_1_diff), .carr(hd_compact_1_carr));
  HD_Compact hd_compact_2 (.x(carryIn), .y(hd_compact_1_diff), .diff(diff), .carr(hd_compact_2_carr));
  or OR1 (carryOut, hd_compact_2_carr, hd_compact_1_carr);

  // Notes on the sheet:
  //   Full Difference
endmodule

// HDc
module HD_Compact (
  input  x,
  input  y,
  output diff,
  output carr
);

  wire not_1_out;

  not not_1 (not_1_out, x);
  xor XOR1 (diff, x, y);
  and AND1 (carr, y, not_1_out);

  // Notes on the sheet:
  //   Compact Half Difference
endmodule

module EC (
  input  x,
  input  y,
  output s
);

  xnor XNOR1 (s, x, y);

  // Notes on the sheet:
  //   Equality Comparator
endmodule

module IC (
  input  x,
  input  y,
  output s
);

  xor XOR1 (s, x, y);

  // Notes on the sheet:
  //   Inequality Comparator
endmodule
