// Logisim project Guia_1103.circ as structural Verilog: 1 circuit, main circuit main
module main (
  input  pulso,
  input  CLR,
  output [1:0] out_3
);

  wire and_1_out, CLK_out, counter_1_carry, d_ff_1_q, d_ff_1_qn, d_ff_2_q, d_ff_3_q, d_ff_3_qn, d_ff_4_q,
       not_1_out;

  Clock CLK (.out(CLK_out));
  D_Flip_Flop #(.enable("true")) d_ff_1 (
    .clk(CLK_out), .D(pulso), .Q(d_ff_1_q), .Qn(d_ff_1_qn), .en(not_1_out), .reset(CLR));  // open: preset
  D_Flip_Flop #(.enable("true")) d_ff_2 (
    .clk(CLK_out), .D(d_ff_1_q), .Q(d_ff_2_q), .en(not_1_out), .reset(CLR));  // open: Qn, preset
  D_Flip_Flop #(.enable("true")) d_ff_3 (
    .clk(CLK_out), .D(d_ff_2_q), .Q(d_ff_3_q), .Qn(d_ff_3_qn), .en(not_1_out), .reset(CLR));  // open: preset
  D_Flip_Flop #(.enable("true")) d_ff_4 (
    .clk(CLK_out), .D(d_ff_3_q), .Q(d_ff_4_q), .en(not_1_out), .reset(CLR));  // open: Qn, preset
  and and_1 (and_1_out, d_ff_4_q, d_ff_3_qn, d_ff_2_q, d_ff_1_qn);
  not not_1 (not_1_out, counter_1_carry);
  Counter #(.width(2), .max('h3)) counter_1 (
    .count(not_1_out), .Q(out_3), .carry(counter_1_carry), .clk(and_1_out), .clr(CLR));  // open: load, D, preset, down
endmodule
