// Logisim project Guia_13.circ as structural Verilog
module AC_DOWN_JK_6_bits (
  input  _1,
  input  Clear
);

  wire j_k_ff_1_qn, j_k_ff_2_qn, j_k_ff_3_qn, j_k_ff_4_qn, j_k_ff_5_qn, j_k_ff_6_qn, Pulse_out;

  Button Pulse (.out(Pulse_out));
  // Probe on j_k_ff_1_qn
  J_K_Flip_Flop j_k_ff_1 (.J(_1), .clk(j_k_ff_2_qn), .K(_1), .Qn(j_k_ff_1_qn), .reset(Clear));  // open: Q, preset
  J_K_Flip_Flop j_k_ff_2 (.J(_1), .clk(j_k_ff_3_qn), .K(_1), .Qn(j_k_ff_2_qn), .reset(Clear));  // open: Q, preset
  // Probe on j_k_ff_2_qn
  // Probe on j_k_ff_3_qn
  J_K_Flip_Flop j_k_ff_3 (.J(_1), .clk(j_k_ff_4_qn), .K(_1), .Qn(j_k_ff_3_qn), .reset(Clear));  // open: Q, preset
  // Probe on j_k_ff_4_qn
  J_K_Flip_Flop j_k_ff_4 (.J(_1), .clk(j_k_ff_5_qn), .K(_1), .Qn(j_k_ff_4_qn), .reset(Clear));  // open: Q, preset
  // Probe on j_k_ff_5_qn
  J_K_Flip_Flop j_k_ff_5 (.J(_1), .clk(j_k_ff_6_qn), .K(_1), .Qn(j_k_ff_5_qn), .reset(Clear));  // open: Q, preset
  J_K_Flip_Flop j_k_ff_6 (.J(_1), .clk(Pulse_out), .K(_1), .Qn(j_k_ff_6_qn), .reset(Clear));  // open: Q, preset
  // Probe on j_k_ff_6_qn

  // Notes on the sheet:
  //   Contador Assíncrono Decrescente de 6 bits
endmodule

module AC_UP_JK_6_bits (
  input  _1,
  input  Clear
);

  wire j_k_ff_1_qn, j_k_ff_2_q, j_k_ff_2_qn, j_k_ff_3_q, j_k_ff_3_qn, j_k_ff_4_q, j_k_ff_4_qn, j_k_ff_5_q,
       j_k_ff_5_qn, j_k_ff_6_q, j_k_ff_6_qn, Pulse_out;

  Button Pulse (.out(Pulse_out));
  // Probe on j_k_ff_1_qn
  J_K_Flip_Flop j_k_ff_1 (.J(_1), .clk(j_k_ff_2_q), .K(_1), .Qn(j_k_ff_1_qn), .reset(Clear));  // open: Q, preset
  J_K_Flip_Flop j_k_ff_2 (
    .J(_1), .clk(j_k_ff_3_q), .K(_1), .Q(j_k_ff_2_q), .Qn(j_k_ff_2_qn), .reset(Clear));  // open: preset
  // Probe on j_k_ff_2_qn
  // Probe on j_k_ff_3_qn
  J_K_Flip_Flop j_k_ff_3 (
    .J(_1), .clk(j_k_ff_4_q), .K(_1), .Q(j_k_ff_3_q), .Qn(j_k_ff_3_qn), .reset(Clear));  // open: preset
  // Probe on j_k_ff_4_qn
  J_K_Flip_Flop j_k_ff_4 (
    .J(_1), .clk(j_k_ff_5_q), .K(_1), .Q(j_k_ff_4_q), .Qn(j_k_ff_4_qn), .reset(Clear));  // open: preset
  // Probe on j_k_ff_5_qn
  J_K_Flip_Flop j_k_ff_5 (
    .J(_1), .clk(j_k_ff_6_q), .K(_1), .Q(j_k_ff_5_q), .Qn(j_k_ff_5_qn), .reset(Clear));  // open: preset
  J_K_Flip_Flop j_k_ff_6 (
    .J(_1), .clk(Pulse_out), .K(_1), .Q(j_k_ff_6_q), .Qn(j_k_ff_6_qn), .reset(Clear));  // open: preset
  // Probe on j_k_ff_6_qn

  // Notes on the sheet:
  //   Contador Assíncrono Crescente de 6 bits
endmodule

module ADC_UP_JK_4_bits (
  input  _1,
  input  Clear
);

  wire and_1_out, and_2_out, j_k_ff_1_q, j_k_ff_1_qn, j_k_ff_2_q, j_k_ff_2_qn, j_k_ff_3_q, j_k_ff_3_qn,
       j_k_ff_4_q, not_1_out, not_2_out, Pulse_out;

  Button Pulse (.out(Pulse_out));
  and and_1 (and_1_out, Clear, and_2_out);
  and and_2 (and_2_out, j_k_ff_1_q, not_1_out, j_k_ff_3_q, not_2_out);
  // Probe on j_k_ff_4_q
  J_K_Flip_Flop j_k_ff_1 (
    .J(_1), .clk(Pulse_out), .K(_1), .Q(j_k_ff_1_q), .Qn(j_k_ff_1_qn), .reset(and_1_out));  // open: preset
  not not_1 (not_1_out, j_k_ff_2_q);
  not not_2 (not_2_out, j_k_ff_4_q);
  // Probe on j_k_ff_3_q
  J_K_Flip_Flop j_k_ff_2 (
    .J(_1), .clk(j_k_ff_1_qn), .K(_1), .Q(j_k_ff_2_q), .Qn(j_k_ff_2_qn), .reset(and_1_out));  // open: preset
  // Probe on j_k_ff_2_q
  J_K_Flip_Flop j_k_ff_3 (
    .J(_1), .clk(j_k_ff_2_qn), .K(_1), .Q(j_k_ff_3_q), .Qn(j_k_ff_3_qn), .reset(and_1_out));  // open: preset
  // Probe on j_k_ff_1_q
  J_K_Flip_Flop j_k_ff_4 (.J(_1), .clk(j_k_ff_3_qn), .K(_1), .Q(j_k_ff_4_q), .reset(and_1_out));  // open: Qn, preset

  // Notes on the sheet:
  //   Contador Assíncrono Decádico Crescente de 4 bits
endmodule

module ADC_DOWN_JK_4_bits (
  input  _1
);

  wire and_1_out, j_k_ff_1_q, j_k_ff_1_qn, j_k_ff_2_q, j_k_ff_2_qn, j_k_ff_3_q, j_k_ff_3_qn, j_k_ff_4_q,
       j_k_ff_4_qn, not_1_out, not_2_out, not_3_out, or_1_out, Pulse_out;

  Button Pulse (.out(Pulse_out));
  not not_1 (not_1_out, _1);
  or or_1 (or_1_out, not_1_out, and_1_out);
  not not_2 (not_2_out, j_k_ff_2_qn);
  and and_1 (and_1_out, j_k_ff_1_qn, not_2_out, j_k_ff_3_qn, not_3_out);
  not not_3 (not_3_out, j_k_ff_4_qn);
  // Probe on j_k_ff_4_q
  J_K_Flip_Flop j_k_ff_1 (
    .J(_1), .clk(Pulse_out), .K(_1), .Q(j_k_ff_1_q), .Qn(j_k_ff_1_qn), .reset(or_1_out));  // open: preset
  // Probe on j_k_ff_3_q
  J_K_Flip_Flop j_k_ff_2 (
    .J(_1), .clk(j_k_ff_1_q), .K(_1), .Q(j_k_ff_2_q), .Qn(j_k_ff_2_qn), .reset(or_1_out));  // open: preset
  // Probe on j_k_ff_2_q
  J_K_Flip_Flop j_k_ff_3 (
    .J(_1), .clk(j_k_ff_2_q), .K(_1), .Q(j_k_ff_3_q), .Qn(j_k_ff_3_qn), .reset(or_1_out));  // open: preset
  // Probe on j_k_ff_1_q
  J_K_Flip_Flop j_k_ff_4 (
    .J(_1), .clk(j_k_ff_3_q), .K(_1), .Q(j_k_ff_4_q), .Qn(j_k_ff_4_qn), .reset(or_1_out));  // open: preset

  // Notes on the sheet:
  //   Contador Assíncrono Decádico Decrescente de 4 bits
endmodule

module SC_T_M7 (
  input  Clear
);

  wire and_1_out, Clock_out, or_1_out, t_ff_1_q, t_ff_2_q, t_ff_2_qn, t_ff_3_q, t_ff_3_qn;

  Clock Clock (.out(Clock_out));
  or or_1 (or_1_out, Clear, and_1_out);
  // Probe on t_ff_1_q
  T_Flip_Flop t_ff_1 (.clk(t_ff_2_qn), .T(t_ff_2_qn), .Q(t_ff_1_q), .reset(or_1_out));  // open: Qn, preset
  and and_1 (and_1_out, t_ff_1_q, t_ff_2_q, t_ff_3_q);
  // Probe on t_ff_2_q
  T_Flip_Flop t_ff_2 (.clk(t_ff_3_qn), .T(t_ff_3_qn), .Q(t_ff_2_q), .Qn(t_ff_2_qn), .reset(or_1_out));  // open: preset
  T_Flip_Flop t_ff_3 (.clk(Clock_out), .T(Clock_out), .Q(t_ff_3_q), .Qn(t_ff_3_qn), .reset(or_1_out));  // open: preset
  // Probe on t_ff_3_q

  // Notes on the sheet:
  //   Contador Síncrono Módulo 7
endmodule

module RC_JK_6_bits (
  input  Input,
  input  Clear
);

  wire Clock_out, j_k_ff_1_q, j_k_ff_1_qn, j_k_ff_2_q, j_k_ff_2_qn, j_k_ff_3_q, j_k_ff_3_qn, j_k_ff_4_q,
       j_k_ff_4_qn, j_k_ff_5_q, j_k_ff_5_qn, j_k_ff_6_q, not_1_out, or_1_out;

  Clock Clock (.out(Clock_out));
  or or_1 (or_1_out, j_k_ff_6_q, Input);
  not not_1 (not_1_out, or_1_out);
  J_K_Flip_Flop j_k_ff_1 (
    .J(or_1_out), .clk(Clock_out), .K(not_1_out), .Q(j_k_ff_1_q), .Qn(j_k_ff_1_qn), .reset(Clear));  // open: preset
  J_K_Flip_Flop j_k_ff_2 (
    .J(j_k_ff_1_q), .clk(Clock_out), .K(j_k_ff_1_qn), .Q(j_k_ff_2_q), .Qn(j_k_ff_2_qn), .reset(Clear));  // open: preset
  J_K_Flip_Flop j_k_ff_3 (
    .J(j_k_ff_2_q), .clk(Clock_out), .K(j_k_ff_2_qn), .Q(j_k_ff_3_q), .Qn(j_k_ff_3_qn), .reset(Clear));  // open: preset
  J_K_Flip_Flop j_k_ff_4 (
    .J(j_k_ff_3_q), .clk(Clock_out), .K(j_k_ff_3_qn), .Q(j_k_ff_4_q), .Qn(j_k_ff_4_qn), .reset(Clear));  // open: preset
  // Probe on j_k_ff_1_q
  // Probe on j_k_ff_2_q
  // Probe on j_k_ff_3_q
  // Probe on j_k_ff_4_q
  J_K_Flip_Flop j_k_ff_5 (
    .J(j_k_ff_4_q), .clk(Clock_out), .K(j_k_ff_4_qn), .Q(j_k_ff_5_q), .Qn(j_k_ff_5_qn), .reset(Clear));  // open: preset
  // Probe on j_k_ff_5_q
  // Probe on j_k_ff_6_q
  J_K_Flip_Flop j_k_ff_6 (
    .J(j_k_ff_5_q), .clk(Clock_out), .K(j_k_ff_5_qn), .Q(j_k_ff_6_q), .reset(Clear));  // open: Qn, preset

  // Notes on the sheet:
  //   Contador em Anel de 6 bits
endmodule

module TRC_JK_6_bits (
  input  Input,
  input  Clear
);

  wire Clock_out, j_k_ff_1_q, j_k_ff_1_qn, j_k_ff_2_q, j_k_ff_2_qn, j_k_ff_3_q, j_k_ff_3_qn, j_k_ff_4_q,
       j_k_ff_4_qn, j_k_ff_5_q, j_k_ff_5_qn, j_k_ff_6_q, j_k_ff_6_qn, not_1_out, or_1_out;

  Clock Clock (.out(Clock_out));
  or or_1 (or_1_out, Input, j_k_ff_6_qn);
  not not_1 (not_1_out, or_1_out);
  J_K_Flip_Flop j_k_ff_1 (
    .J(or_1_out), .clk(Clock_out), .K(not_1_out), .Q(j_k_ff_1_q), .Qn(j_k_ff_1_qn), .reset(Clear));  // open: preset
  J_K_Flip_Flop j_k_ff_2 (
    .J(j_k_ff_1_q), .clk(Clock_out), .K(j_k_ff_1_qn), .Q(j_k_ff_2_q), .Qn(j_k_ff_2_qn), .reset(Clear));  // open: preset
  J_K_Flip_Flop j_k_ff_3 (
    .J(j_k_ff_2_q), .clk(Clock_out), .K(j_k_ff_2_qn), .Q(j_k_ff_3_q), .Qn(j_k_ff_3_qn), .reset(Clear));  // open: preset
  J_K_Flip_Flop j_k_ff_4 (
    .J(j_k_ff_3_q), .clk(Clock_out), .K(j_k_ff_3_qn), .Q(j_k_ff_4_q), .Qn(j_k_ff_4_qn), .reset(Clear));  // open: preset
  // Probe on j_k_ff_1_q
  // Probe on j_k_ff_3_q
  // Probe on j_k_ff_2_q
  // Probe on j_k_ff_4_q
  J_K_Flip_Flop j_k_ff_5 (
    .J(j_k_ff_4_q), .clk(Clock_out), .K(j_k_ff_4_qn), .Q(j_k_ff_5_q), .Qn(j_k_ff_5_qn), .reset(Clear));  // open: preset
  // Probe on j_k_ff_5_q
  // Probe on j_k_ff_6_q
  J_K_Flip_Flop j_k_ff_6 (
    .J(j_k_ff_5_q), .clk(Clock_out), .K(j_k_ff_5_qn), .Q(j_k_ff_6_q), .Qn(j_k_ff_6_qn), .reset(Clear));  // open: preset

  // Notes on the sheet:
  //   Contador em Anel Torcido de 6 bits
endmodule
