// Logisim project Guia_17.circ as structural Verilog: 6 circuits, main circuit main
module main (
);


  // Notes on the sheet:
  //   As resoluções de todas as questões foram feitas neste único arquivo.
endmodule

module Q1 (
  input  a,
  input  b,
  input  c
);

  wire and_1_out, and_2_out, CLK_out, CLR_out, Da_q, Db_q, not_1_out;

  Clock CLK (.out(CLK_out));
  Button CLR (.out(CLR_out));
  and and_1 (and_1_out, b, c);
  // Probe on Da_q
  D_Flip_Flop Da (.clk(CLK_out), .D(and_1_out), .Q(Da_q), .reset(CLR_out));  // open: Qn, preset
  and and_2 (and_2_out, not_1_out, c);
  // Probe on Db_q
  D_Flip_Flop Db (.clk(CLK_out), .D(and_2_out), .Q(Db_q), .reset(CLR_out));  // open: Qn, preset
  not not_1 (not_1_out, a);
endmodule

module Q2 (
  input  a,
  input  b,
  input  c
);

  wire CLK_out, CLR_out, JK_to_SR_2_q, JK_to_SR_q, not_1_out, not_2_out, Ra_out, Rb_out, Sa_out, Sb_out;

  Clock CLK (.out(CLK_out));
  Button CLR (.out(CLR_out));
  and Sa (Sa_out, a, c);
  and Ra (Ra_out, not_1_out, c);
  // Probe on JK_to_SR_q
  J_K_Flip_Flop JK_to_SR (.J(Sa_out), .clk(CLK_out), .K(Ra_out), .Q(JK_to_SR_q), .reset(CLR_out));  // open: Qn, preset
  not not_1 (not_1_out, a);
  and Sb (Sb_out, b, c);
  and Rb (Rb_out, not_2_out, c);
  // Probe on JK_to_SR_2_q
  J_K_Flip_Flop JK_to_SR_2 (
    .J(Sb_out), .clk(CLK_out), .K(Rb_out), .Q(JK_to_SR_2_q), .reset(CLR_out));  // open: Qn, preset
  not not_2 (not_2_out, b);
endmodule

module Q3 (
  input  a,
  input  b,
  input  c
);

  wire and_1_out, and_2_out, and_3_out, and_4_out, CLK_out, CLR_out, JK_to_T_2_q, JK_to_T_q, not_1_out,
       not_2_out, not_3_out, not_4_out, Ta_out, Tb_out;

  Clock CLK (.out(CLK_out));
  Button CLR (.out(CLR_out));
  and and_1 (and_1_out, not_1_out, b, c);
  or Ta (Ta_out, and_1_out, and_2_out);
  and and_2 (and_2_out, a, not_2_out, c);
  // Probe on JK_to_T_q
  J_K_Flip_Flop JK_to_T (.J(Ta_out), .clk(CLK_out), .K(Ta_out), .Q(JK_to_T_q), .reset(CLR_out));  // open: Qn, preset
  not not_1 (not_1_out, a);
  not not_2 (not_2_out, b);
  or Tb (Tb_out, and_3_out, and_4_out);
  // Probe on JK_to_T_2_q
  J_K_Flip_Flop JK_to_T_2 (
    .J(Tb_out), .clk(CLK_out), .K(Tb_out), .Q(JK_to_T_2_q), .reset(CLR_out));  // open: Qn, preset
  not not_3 (not_3_out, a);
  not not_4 (not_4_out, b);
  and and_3 (and_3_out, not_3_out, not_4_out, c);
  and and_4 (and_4_out, a, b, c);
endmodule

module Q4 (
  input  CLR,
  output [2:0] \output 
);

  wire CLK_out;

  Clock CLK (.out(CLK_out));
  T_Flip_Flop t_ff_1 (.clk(CLK_out), .T(1'b1), .Q(\output [0]), .reset(CLR));  // open: Qn, preset
  T_Flip_Flop t_ff_2 (.clk(\output [0]), .T(1'b1), .Q(\output [1]), .reset(CLR));  // open: Qn, preset
  T_Flip_Flop t_ff_3 (.clk(\output [1]), .T(1'b1), .Q(\output [2]), .reset(CLR));  // open: Qn, preset

  // Notes on the sheet:
  //   input
endmodule

module Q5 (
  input  CLR,
  output [2:0] \output 
);

  wire CLK_out, t_ff_1_qn, t_ff_2_qn;

  Clock CLK (.out(CLK_out));
  T_Flip_Flop t_ff_1 (.clk(CLK_out), .T(1'b1), .Q(\output [0]), .Qn(t_ff_1_qn), .reset(CLR));  // open: preset
  T_Flip_Flop t_ff_2 (.clk(t_ff_1_qn), .T(1'b1), .Q(\output [1]), .Qn(t_ff_2_qn), .reset(CLR));  // open: preset
  T_Flip_Flop t_ff_3 (.clk(t_ff_2_qn), .T(1'b1), .Q(\output [2]), .reset(CLR));  // open: Qn, preset

  // Notes on the sheet:
  //   input
endmodule
